# Fritzing sketch AnalogRelay (saved by Fritzing 0.8.5b)
circuit board: 6.9215cm x 5.33756cm
breadboards: 1

parts:
  K1 = Relay [part_number=FRS1B-S package=THT]
  R3 = Resistor [resistance=220 tolerance=±5% package=THT]
  D2 = Rectifier Diode [part_number=1N4001 package="300 mil [THT]"]
  S1 = Pushbutton [package="[THT]"]
  VCC1 = Battery block 9V  # not connected
  VCC1_2 = Battery block 9V
  Q2 = NPN-Transistor [package="TO92 [THT]"]
  M1 = DC Motor

nets:
  N1: K1.A, M1.pin_1
  N2: K1.COIL1, D2.anode, Q2.C
  N3: K1.C1, K1.C2
  N4: K1.COIL2, D2.cathode, S1.Pin_1, S1.Pin_2, VCC1_2.+
  N5: R3.Pin_0, Q2.B
  N6: R3.Pin_1, S1.Pin_3, S1.Pin_4
  N7: VCC1_2.-, Q2.E
