# Fritzing sketch ArduinPicoButton (saved by Fritzing 0.8.5b)
breadboards: 1

parts:
  R2 = Resistor [resistance=10k tolerance=±5% package=THT]
  Arduino2 = Modified Pico
  S3 = Pushbutton [package="[THT]"]
  LED2 = LED - 5mm [color="Red (633nm)" package="5 mm [THT]"]

nets:
  N1: R2.Pin_0, LED2.cathode
  N2: R2.Pin_1, Arduino2.D2, S3.Pin_3, S3.Pin_4
  N3: Arduino2.D13, LED2.anode
  N4: S3.Pin_1, S3.Pin_2
