# Fritzing sketch BasicLEDMosfetSwitch (saved by Fritzing 0.4.3b)
breadboards: 1

parts:
  R1 = Resistor [resistance=1k package=THT]
  VCC1 = obsolete Battery
  LED1 = Red LED - 5mm
  VCC1_2 = obsolete Battery
  S1 = Pushbutton [package="[THT]"]
  Q1 = Basic FET N-Channel [package="TO220 [THT]"]
  R2 = Resistor [resistance=10k package=THT]
  R3 = Resistor [resistance=1k package=THT]
  LED1_2 = Red LED - 5mm

nets:
  N1: R1.Pin_0, S1.Pin_3, S1.Pin_4
  N2: R1.Pin_1, LED1.anode
  N3: VCC1.-, Q1.source, R2.Pin_1
  N4: VCC1.+, S1.Pin_1, S1.Pin_2
  N5: LED1.cathode, Q1.gate, R2.Pin_0
  N6: VCC1_2.+, LED1_2.cathode
  N7: Q1.drain, R3.Pin_1
  N8: R3.Pin_0, LED1_2.anode
