# Fritzing sketch BasicLEDMosfetSwitch (saved by Fritzing 0.8.5b)
breadboards: 1

parts:
  R1 = Resistor [resistance=1k tolerance=±5% package=THT]
  S1 = Pushbutton [package="[THT]"]
  Q1 = Basic FET N-Channel [package="TO220 [THT]"]
  R2 = Resistor [resistance=10k tolerance=±5% package=THT]
  R3 = Resistor [resistance=1k tolerance=±5% package=THT]
  VCC1 = Battery
  LED1 = LED - 5mm [color="Red (633nm)" package="5 mm [THT]"]
  VCC1_2 = Battery
  LED1_2 = LED - 5mm [color="Red (633nm)" package="5 mm [THT]"]

nets:
  N1: R1.Pin_0, S1.Pin_3, S1.Pin_4
  N2: R1.Pin_1, LED1.anode
  N3: S1.Pin_1, S1.Pin_2
  N4: Q1.gate, R2.Pin_0, LED1.cathode
  N5: Q1.drain, R3.Pin_1
  N6: Q1.source, R2.Pin_1, VCC1.-, VCC1_2.-
  N7: R3.Pin_0, LED1_2.anode
  N8: VCC1.+, LED1_2.cathode
