# Fritzing sketch BasicLEDPattern (saved by Fritzing 0.5.2b)
breadboards: 1

parts:
  VCC1 = obsolete Battery
  LED1 = Red LED - 5mm
  S1 = Tilt Switch [package=THT]  # not connected
  R1 = Resistor [resistance=1k package=THT]
  S2 = Pushbutton [package="[THT]"]

nets:
  N1: VCC1.-, LED1.cathode
  N2: VCC1.+, S2.Pin_1, S2.Pin_2
  N3: LED1.anode, R1.Pin_1
  N4: S2.Pin_3, S2.Pin_4
