# Fritzing sketch BasicLEDPattern (saved by Fritzing 0.8.5b)
breadboards: 1

parts:
  R1 = Resistor [resistance=1k tolerance=±5% package=THT]
  S2 = Pushbutton [package="[THT]"]
  LED1 = LED - 5mm [color="Red (633nm)" package="5 mm [THT]"]
  VCC1 = Battery block 9V  # not connected

nets:
  N1: R1.Pin_1, LED1.anode
  N2: S2.Pin_1, S2.Pin_2
  N3: S2.Pin_3, S2.Pin_4
