# Fritzing sketch BasicLEDPhotoresistor (saved by Fritzing 0.8.5b)
breadboards: 1

parts:
  R1 = Resistor [resistance=1k tolerance=±5% package=THT]
  R2 = Photocell (LDR) [package=THT]
  VCC1 = Battery block 9V
  LED1 = LED - 5mm [color="Red (633nm)" package="5 mm [THT]"]

nets:
  N1: R1.Pin_0, R2.pin_0
  N2: R1.Pin_1, LED1.anode
  N3: R2.pin_1, VCC1.+
  N4: VCC1.-, LED1.cathode
