# Fritzing sketch BasicLEDPotentionmeter (saved by Fritzing 0.4.3b)
breadboards: 1

parts:
  R1 = Resistor [resistance=1k package=THT]
  LED1 = Red LED - 5mm
  R2 = Rotary Potentiometer (Large) [package=THT]
  VCC1 = Battery block 9V

nets:
  N1: R1.Pin_0, R2.wiper
  N2: R1.Pin_1, LED1.anode
  N3: LED1.cathode, R2.leg1, VCC1.-
  N4: R2.leg2, VCC1.+
