# Fritzing sketch BasicLEDPotentionmeter (saved by Fritzing 0.8.5b)
breadboards: 1

parts:
  R1 = Resistor [resistance=1k tolerance=±5% package=THT]
  LED1 = LED - 5mm [color="Red (633nm)" package="5 mm [THT]"]
  VCC1 = Battery block 9V
  POT1 = Breadboard Trimpot

nets:
  N1: R1.Pin_0, POT1.PIN2
  N2: R1.Pin_1, LED1.anode
  N3: VCC1.-, POT1.PIN1
  N4: VCC1.+, POT1.PIN3
