# Fritzing sketch BasicLEDPotentionmeterBreadboardable (saved by Fritzing 0.8.5b)
breadboards: 1

parts:
  R1 = Resistor [resistance=1k tolerance=±5% package=THT]
  R2 = Rotary Potentiometer (Small) [maximum_resistance=100kΩ package=THT]
  LED1 = LED - 5mm [color="Red (633nm)" package="5 mm [THT]"]
  VCC1 = Battery block 9V

nets:
  N1: R1.Pin_0, R2.wiper
  N2: R1.Pin_1, LED1.anode
  N3: R2.leg1, LED1.cathode, VCC1.-
  N4: R2.leg2, VCC1.+
