# Fritzing sketch BasicLEDReedSwitch (saved by Fritzing 0.4.3b)
breadboards: 1

parts:
  R1 = Resistor [resistance=1k package=THT]
  LED1 = Red LED - 5mm
  S1 = Reed switch [package=THT]
  VCC1 = Battery block 9V

nets:
  N1: R1.Pin_0, S1.pin_1
  N2: R1.Pin_1, LED1.anode
  N3: LED1.cathode, VCC1.-
  N4: S1.pin_2, VCC1.+
