# Fritzing sketch BasicLEDTiltSwitch (saved by Fritzing 0.5.2b)
breadboards: 1

parts:
  R1 = Resistor [resistance=1k package=THT]
  VCC1 = Battery block 9V
  LED1 = Red LED - 5mm
  S1 = Tilt Switch [package=THT]

nets:
  N1: R1.Pin_0, S1.Pin_1
  N2: R1.Pin_1, LED1.anode
  N3: VCC1.-, LED1.cathode
  N4: VCC1.+, S1.Pin_2
