# Fritzing sketch BasicLEDTiltSwitch (saved by Fritzing 0.8.5b)
breadboards: 1

parts:
  R1 = Resistor [resistance=330 tolerance=±5% package=THT]
  S1 = Tilt Switch [package=THT]
  VCC1 = Battery block 9V
  LED1 = LED - 5mm [color="Red (633nm)" package="5 mm [THT]"]

nets:
  N1: R1.Pin_0, S1.Pin_1
  N2: R1.Pin_1, LED1.anode
  N3: S1.Pin_2, VCC1.+
  N4: VCC1.-, LED1.cathode
