# Fritzing sketch ButtonPullDown (saved by Fritzing 0.8.5b)
breadboards: 1

parts:
  R1 = Resistor [resistance=1k tolerance=±5% package=THT]
  R2 = Resistor [resistance=220 tolerance=±5% package=THT]
  VCC1 = Battery block 9V
  LED1 = LED - 5mm [color="Red (633nm)" package="5 mm [THT]"]
  S1 = Pushbutton [package="[THT]"]

nets:
  N1: R1.Pin_0, LED1.anode
  N2: R1.Pin_1, R2.Pin_1, VCC1.+, LED1.cathode
  N3: R2.Pin_0, S1.Pin_1, S1.Pin_2
  N4: VCC1.-, S1.Pin_3, S1.Pin_4
