# Fritzing sketch CapacitorParallelLED (saved by Fritzing 0.4.3b)
breadboards: 1

parts:
  S1 = Pushbutton [package="[THT]"]
  R1 = Resistor [resistance=1k package=THT]
  LED1 = Red LED - 5mm
  VCC1 = Battery block 9V
  C1 = Electrolytic Capacitor [package=THT]

nets:
  N1: S1.Pin_1, S1.Pin_2, R1.Pin_0
  N2: S1.Pin_3, S1.Pin_4, LED1.anode
  N3: R1.Pin_1, VCC1.+, C1.+
  N4: LED1.cathode, VCC1.-, C1.-
