# Fritzing sketch CapacitorParallelLED (saved by Fritzing 0.8.5b)
breadboards: 1

parts:
  S1 = Pushbutton [package="[THT]"]
  R1 = Resistor [resistance=1k tolerance=±5% package=THT]
  VCC1 = Battery block 9V
  LED1 = LED - 5mm [color="Red (633nm)" package="5 mm [THT]"]
  C1 = Electrolytic Capacitor [capacitance=1000µF package="300 mil [THT, electrolytic]"]

nets:
  N1: S1.Pin_1, S1.Pin_2, R1.Pin_0
  N2: S1.Pin_3, S1.Pin_4, LED1.anode
  N3: R1.Pin_1, VCC1.+, C1.+
  N4: VCC1.-, LED1.cathode, C1.-
