# Fritzing sketch CapictorInSeriesandParallel (saved by Fritzing 0.5.2b)
breadboards: 1

parts:
  S1 = Pushbutton [package="[THT]"]
  R1 = Resistor [resistance=1k package=THT]
  LED1 = Red LED - 5mm
  S2 = Pushbutton [package="[THT]"]
  VCC1 = Battery block 9V
  C1 = Electrolytic Capacitor [package=THT]
  C2 = Electrolytic Capacitor [package=THT]

nets:
  N1: S1.Pin_1, S1.Pin_2, C1.+
  N2: S1.Pin_3, S1.Pin_4, C2.+
  N3: R1.Pin_0, C2.-
  N4: R1.Pin_1, LED1.anode
  N5: LED1.cathode, S2.Pin_1, S2.Pin_2, C1.-
  N6: S2.Pin_3, S2.Pin_4, VCC1.-
