# Fritzing sketch CapictorInSeriesandParallel (saved by Fritzing 0.8.5b)
breadboards: 1

parts:
  S1 = Pushbutton [package="[THT]"]
  R1 = Resistor [resistance=1k tolerance=±5% package=THT]
  S2 = Pushbutton [package="[THT]"]
  C1 = Electrolytic Capacitor [capacitance=1000µF package="300 mil [THT, electrolytic]"]
  LED1 = LED - 5mm [color="Red (633nm)" package="5 mm [THT]"]
  C2 = Electrolytic Capacitor [capacitance=1µF package="100 mil [THT, electrolytic]"]
  VCC1 = Battery block 9V

nets:
  N1: S1.Pin_1, S1.Pin_2, C1.+
  N2: S1.Pin_3, S1.Pin_4, C2.+
  N3: R1.Pin_0, C2.-
  N4: R1.Pin_1, LED1.anode
  N5: S2.Pin_1, S2.Pin_2, C1.-, LED1.cathode
  N6: S2.Pin_3, S2.Pin_4, VCC1.-
