# Fritzing sketch DARLINGTON (saved by Fritzing 0.8.5b)
circuit board: 5.70089cm x 5.61622cm
breadboards: 1

parts:
  R1 = Resistor [resistance=220k tolerance=±5% package=THT]
  R2 = Resistor [resistance=1k tolerance=±5% package=THT]
  S1 = Toggle Switch [package=THT]
  J1 = female pin header, 1 pin [form="♂ (male)"]
  J3 = female pin header, 1 pin [form="♂ (male)"]
  VCC1 = Battery
  Q1 = NPN-Transistor [package="TO92 [THT]"]
  Q2 = NPN-Transistor [package="TO92 [THT]"]
  LED1 = LED - 5mm [color="Red (633nm)" package="5 mm [THT]"]

nets:
  N1: R1.Pin_0, J1.pin1
  N2: R1.Pin_1, Q1.B
  N3: R2.Pin_0, LED1.anode
  N4: R2.Pin_1, S1.COM
  N5: S1.L1, J3.pin1, VCC1.+
  N6: VCC1.-, Q2.E
  N7: Q1.E, Q2.B
  N8: Q1.C, Q2.C, LED1.cathode

notes:
  "Darlington pair" - while holding one finger to the male connector by the 220K resistor, touch the male connector by the positive terminal - the LED should light up.
  DARLINGTON
