# Fritzing sketch HallEffectSensor (saved by Fritzing 0.8.5b)
breadboards: 1

parts:
  VCC1 = Battery block 9V
  HallEffect = mystery part, 3 pins [chip_label=? spacing=300mil]
  R1 = Resistor [tolerance=±5% resistance=220 package=THT]
  LED1 = LED - 5mm [color="Red (633nm)" package="5 mm [THT]"]

nets:
  N1: VCC1.-, HallEffect.pin2
  N2: VCC1.+, HallEffect.pin1, LED1.anode
  N3: HallEffect.pin3, R1.Pin_0
  N4: R1.Pin_1, LED1.cathode
