# Fritzing sketch LEDTransitorBlink (saved by Fritzing 0.8.5b)
breadboards: 1

parts:
  Q1 = npn-Powertransistor [package="TO220 [THT]"]
  R1 = Resistor [resistance=220 tolerance=±5% package=THT]
  S1 = Pushbutton [package="[THT]"]
  R1_2 = Resistor [resistance=220 tolerance=±5% package=THT]
  Q1_2 = npn-Powertransistor [package="TO220 [THT]"]
  Q1_3 = npn-Powertransistor [package="TO220 [THT]"]  # not connected
  LED1 = LED - 5mm [color="Red (633nm)" package="5 mm [THT]"]
  C1 = Electrolytic Capacitor [capacitance=1000µF package="300 mil [THT, electrolytic]"]
  C1_2 = Electrolytic Capacitor [capacitance=1000µF package="300 mil [THT, electrolytic]"]
  VCC1 = Battery
  LED1_2 = LED - 5mm [color="Red (633nm)" package="5 mm [THT]"]

nets:
  N1: Q1.collector, R1.Pin_1, C1_2.+
  N2: Q1.emitter, R1_2.Pin_1, Q1_2.emitter, C1_2.-, VCC1.-
  N3: R1.Pin_0, LED1.anode
  N4: S1.Pin_1, S1.Pin_2, VCC1.+
  N5: S1.Pin_3, S1.Pin_4, C1.+
  N6: R1_2.Pin_0, LED1_2.anode
  N7: Q1_2.base, C1.-
  N8: Q1_2.collector, LED1_2.cathode
