# Fritzing sketch NewBasicLED (saved by Fritzing 0.8.5b)
breadboards: 1

parts:
  VCC1 = Battery block 9V
  LED1 = LED - 5mm [color="Red (633nm)" package="5 mm [THT]"]
  R1 = Resistor [tolerance=±5% resistance=220 package=THT]
  LED2 = LED - 5mm [color="Red (633nm)" package="5 mm [THT]"]
  R2 = Resistor [tolerance=±5% resistance=220 package=THT]

nets (from the breadboard view):
  N1: VCC1.-, LED1.cathode, LED2.cathode
  N2: VCC1.+, R1.Pin_1, R2.Pin_1
  N3: LED1.anode, R1.Pin_0
  N4: LED2.anode, R2.Pin_0
