# Fritzing sketch NewBasicMotorWithButton (saved by Fritzing 0.8.5b)
breadboards: 1

parts:
  M1 = DC Motor
  S2 = Pushbutton [package=THT]
  VCC1 = Battery block 9V

nets:
  N1: M1.pin_1, VCC1.+
  N2: M1.pin_2, S2.leg1
  N3: S2.leg0, VCC1.-
