# Fritzing sketch NewTransistorMotorWithButton (saved by Fritzing 0.8.5b)
breadboards: 1

parts:
  S2 = Pushbutton [package=THT]
  M1 = DC Motor
  VCC1 = Battery block 9V
  Q1 = NPN-Transistor [package="TO92 [THT]"]
  R1 = Resistor [tolerance=±5% resistance=1k package="1206 [SMD]"]
  R1_2 = Resistor [tolerance=±5% resistance=1k package="0603 [SMD]"]

nets:
  N1: S2.leg0, R1.Pin_0, R1_2.Pin_0
  N2: S2.leg1, M1.pin_2, VCC1.+
  N3: M1.pin_1, Q1.C
  N4: VCC1.-, Q1.E
  N5: Q1.B, R1.Pin_1, R1_2.Pin_1
