# Fritzing sketch POt (saved by Fritzing 0.8.5b)
breadboards: 1

parts:
  VCC1 = Battery block 9V
  LED2 = LED - 5mm [color="Red (633nm)" package="5 mm [THT]"]
  R1 = Resistor [tolerance=±5% resistance=220 package=THT]
  POT1 = Breadboard Trimpot

nets:
  N1: VCC1.-, LED2.cathode, POT1.PIN1
  N2: VCC1.+, POT1.PIN3
  N3: LED2.anode, R1.Pin_0
  N4: R1.Pin_1, POT1.PIN2
