# Fritzing sketch Relay (saved by Fritzing 0.4.3b)
breadboards: 1

parts:
  K1 = Relay [package=THT]
  M1 = DC Motor
  R3 = Resistor [resistance=220 package=THT]
  Q2 = NPN-Transistor [package="TO92 [THT]"]
  D2 = Rectifier Diode [package="300 mil [THT]"]
  VCC1 = Battery block 9V
  S1 = Pushbutton [package="[THT]"]

nets:
  N1: K1.A, M1.pin_1
  N2: K1.COIL1, Q2.C, D2.anode
  N3: K1.C1, K1.C2, K1.COIL2, D2.cathode, VCC1.+, S1.Pin_1, S1.Pin_2
  N4: M1.pin_2, Q2.E, VCC1.-
  N5: R3.Pin_0, Q2.B
  N6: R3.Pin_1, S1.Pin_3, S1.Pin_4
