# Fritzing sketch SimpleLEDwithButton (saved by Fritzing 0.5.2b)
breadboards: 1

parts:
  LED1 = Red LED - 5mm
  VCC1 = Battery block 9V
  R1 = Resistor [resistance=330 package=THT]
  S1 = Pushbutton [package="[THT]"]

nets:
  N1: LED1.cathode, VCC1.-, VCC1.+, S1.Pin_1, S1.Pin_2
  N2: LED1.anode, R1.Pin_1
  N3: R1.Pin_0, S1.Pin_3, S1.Pin_4
