# Fritzing sketch SimpleLEDwithButton (saved by Fritzing 0.8.5b)
circuit board: 5.64444cm x 3.58422cm
breadboards: 1

parts:
  R1 = Resistor [resistance=330 tolerance=±5% package=THT]
  S1 = Pushbutton [package="[THT]"]
  LED1 = LED - 5mm [color="Red (633nm)" package="5 mm [THT]"]
  VCC1 = Battery block 9V

nets:
  N1: R1.Pin_0, S1.Pin_3, S1.Pin_4
  N2: R1.Pin_1, LED1.anode
  N3: S1.Pin_1, S1.Pin_2, LED1.cathode, VCC1.-, VCC1.+
