# Fritzing sketch SwitchLED (saved by Fritzing 0.8.5b)
breadboards: 1

parts:
  VCC1 = Battery block 9V
  R1 = Resistor [tolerance=±5% resistance=220 package=THT]
  LED1 = LED - 5mm [color="Red (633nm)" package="5 mm [THT]"]
  S1 = Toggle Switch [package=THT]

nets:
  N1: VCC1.-, S1.COM
  N2: VCC1.+, LED1.anode, S1.L1
  N3: R1.Pin_0, S1.L2
  N4: R1.Pin_1, LED1.cathode
