# Fritzing sketch TiltBallLEDSwitch (saved by Fritzing 0.8.5b)
breadboards: 1

parts:
  S1 = Tilt Switch [package=THT]
  R1 = Resistor [resistance=1k tolerance=±5% package=THT]
  LED1 = LED - 5mm [color="Red (633nm)" package="5 mm [THT]"]
  VCC1 = Battery block 9V

nets:
  N1: S1.Pin_1, R1.Pin_0
  N2: S1.Pin_2, VCC1.+
  N3: R1.Pin_1, LED1.anode
  N4: LED1.cathode, VCC1.-
