# Fritzing sketch TouchSwithDarlingtonPair (saved by Fritzing 0.5.2b)
breadboards: 1

parts:
  Q1 = NPN-Transistor [package="TO92 [THT]"]
  Q2 = NPN-Transistor [package="TO92 [THT]"]
  LED1 = Red LED - 5mm [package="5 mm [THT]"]
  R1 = Resistor [resistance=1k package=THT]
  J1 = female pin header, 1 pin [form="♂ (male)"]
  VCC1 = Battery block 9V
  J1_2 = female pin header, 1 pin [form="♂ (male)"]

nets:
  N1: Q1.E, VCC1.-
  N2: Q1.B, Q2.E
  N3: Q1.C, Q2.C, LED1.cathode
  N4: Q2.B, J1.pin1
  N5: LED1.anode, R1.Pin_0
  N6: R1.Pin_1, VCC1.+, J1_2.pin1
