# Fritzing sketch TouchSwithDarlingtonPair (saved by Fritzing 0.8.5b)
breadboards: 1

parts:
  R1 = Resistor [resistance=1k tolerance=±5% package=THT]
  J1 = female pin header, 1 pin [form="♂ (male)"]
  J1_2 = female pin header, 1 pin [form="♂ (male)"]
  Q2 = NPN-Transistor [package="TO92 [THT]"]
  VCC1 = Battery block 9V
  LED1 = LED - 5mm [color="Red (633nm)" package="5 mm [THT]"]
  Q1 = NPN-Transistor [package="TO92 [THT]"]

nets:
  N1: R1.Pin_0, LED1.anode
  N2: R1.Pin_1, J1_2.pin1, VCC1.+
  N3: J1.pin1, Q2.B
  N4: Q2.E, Q1.B
  N5: Q2.C, LED1.cathode, Q1.C
  N6: VCC1.-, Q1.E
