# Fritzing sketch TransistorElectricSwitch (saved by Fritzing 0.8.5b)
breadboards: 1

parts:
  VCC1 = Battery block 9V
  LED1 = LED - 5mm [color="Red (633nm)" package="5 mm [THT]"]
  R1 = Resistor [tolerance=±5% resistance=330 package=THT]
  S1 = Pushbutton [package=THT]
  Q1 = NPN-Transistor [package="TO92 [THT]"]
  R2 = Resistor [tolerance=±5% resistance=1k package=THT]

nets:
  N1: VCC1.-, Q1.E
  N2: VCC1.+, LED1.anode, S1.leg1
  N3: LED1.cathode, R1.Pin_1
  N4: R1.Pin_0, Q1.C
  N5: S1.leg0, R2.Pin_0
  N6: Q1.B, R2.Pin_1
