# Fritzing sketch npnMotorTransistor (saved by Fritzing 0.4.3b)
breadboards: 1

parts:
  R8 = Resistor [resistance=1k package=THT]
  R9 = Resistor [resistance=330 package=THT]
  LED8 = Red LED - 5mm
  VCC1 = Battery block 9V
  S1 = Pushbutton [package="[THT]"]
  Q1 = NPN-Transistor [package="TO92 [THT]"]
  M1 = DC Motor
  D1 = Rectifier Diode [package="300 mil [THT]"]

nets:
  N1: R8.Pin_0, S1.Pin_1, S1.Pin_2
  N2: R8.Pin_1, Q1.B
  N3: R9.Pin_0, LED8.anode
  N4: R9.Pin_1, VCC1.+, S1.Pin_3, S1.Pin_4, M1.pin_2
  N5: LED8.cathode, Q1.C, D1.cathode
  N6: VCC1.-, Q1.E
  N7: M1.pin_1, D1.anode
