# Fritzing sketch npnMotorTransistor (saved by Fritzing 0.8.5b)
breadboards: 1

parts:
  R9 = Resistor [resistance=330 tolerance=±5% package=THT]
  R8 = Resistor [resistance=10k tolerance=±5% package=THT]
  S1 = Pushbutton [package="[THT]"]
  Q1 = NPN-Transistor [package="TO92 [THT]"]
  VCC1 = Battery block 9V
  M1 = DC Motor
  LED8 = LED - 5mm [color="Red (633nm)" package="5 mm [THT]"]
  VCC1_2 = Battery block 9V

nets:
  N1: R9.Pin_0, R8.Pin_1, Q1.E, Q1.B, Q1.C, VCC1.-, LED8.cathode, LED8.anode, VCC1_2.-
  N2: R9.Pin_1, M1.pin_1, M1.pin_2, VCC1_2.+
  N3: R8.Pin_0, S1.Pin_1, S1.Pin_2
  N4: S1.Pin_3, S1.Pin_4, VCC1.+

notes:
  Parts List
  Quantity Part
  1 10k Ohm Resistor
  1 330 Ohm Resistor
  2 Battery block 9V
  1 DC Motor
  1 NPN-Transistor 2n2222
  1 Pushbutton
  1 RSR 03MB102 Breadboard
  1 Red LED -
