# Fritzing sketch npnPowerTransistor (saved by Fritzing 0.8.5b)
circuit board: 6.9215cm x 5.33756cm
breadboards: 1

parts:
  Q1 = npn-Powertransistor [package="TO220 [THT]"]
  R6 = Resistor [resistance=220 tolerance=±5% package=THT]
  R7 = Resistor [resistance=220 tolerance=±5% package=THT]
  R8 = Resistor [resistance=1k tolerance=±5% package=THT]
  R9 = Resistor [resistance=220 tolerance=±5% package=THT]
  R10 = Resistor [resistance=220 tolerance=±5% package=THT]
  LED5 = LED - 5mm [color="Red (633nm)" package="5 mm [THT]"]
  LED7 = LED - 5mm [color="Red (633nm)" package="5 mm [THT]"]
  LED6 = LED - 5mm [color="Red (633nm)" package="5 mm [THT]"]
  LED8 = LED - 5mm [color="Red (633nm)" package="5 mm [THT]"]
  Arduino2 = Arduino Uno (Rev3)

nets:
  N1: Q1.base, R8.Pin_1
  N2: Q1.collector, LED5.cathode, LED7.cathode, LED6.cathode, LED8.cathode
  N3: Q1.emitter, Arduino2.GND
  N4: R6.Pin_0, LED7.anode
  N5: R6.Pin_1, R7.Pin_1, R9.Pin_1, R10.Pin_1
  N6: R7.Pin_0, LED5.anode
  N7: R9.Pin_0, LED8.anode
  N8: R10.Pin_0, LED6.anode

notes:
  Using a power transistor with an Arduino will allow you to control outputs that need more current or higher voltages than the Arduino can provide. Related example: http://itp.nyu.edu/physcomp/Tutorials/HighCurrentLoads
