# Fritzing sketch ArduinPicoButton (saved by Fritzing 0.5.2b)
breadboards: 1

parts:
  R2 = Resistor [resistance=10k package=THT]
  LED2 = Red LED - 5mm [package="5 mm [THT]"]
  Arduino2 = Modified Pico
  S3 = Pushbutton [package="[THT]"]

nets:
  N1: R2.Pin_0, LED2.cathode
  N2: R2.Pin_1, Arduino2.D2, S3.Pin_3, S3.Pin_4
  N3: LED2.anode, Arduino2.D13
  N4: S3.Pin_1, S3.Pin_2
