# Fritzing sketch BasicLEDMosfetSwitch (saved by Fritzing 0.5.2b)
breadboards: 1

parts:
  VCC1 = obsolete Battery
  VCC1_2 = obsolete Battery
  R1 = Resistor [resistance=1k package=THT]
  LED1 = Red LED - 5mm
  LED1_2 = Red LED - 5mm
  S1 = Pushbutton [package="[THT]"]
  Q1 = Basic FET N-Channel [package="TO220 [THT]"]
  R2 = Resistor [resistance=10k package=THT]
  R3 = Resistor [resistance=1k package=THT]

nets:
  N1: VCC1.-, VCC1_2.-, Q1.source, R2.Pin_1
  N2: VCC1_2.+, LED1.cathode
  N3: R1.Pin_0, S1.Pin_3, S1.Pin_4
  N4: R1.Pin_1, LED1_2.anode
  N5: LED1.anode, R3.Pin_0
  N6: LED1_2.cathode, Q1.gate, R2.Pin_0
  N7: S1.Pin_1, S1.Pin_2
  N8: Q1.drain, R3.Pin_1
