# Fritzing sketch ButtonPullDown (saved by Fritzing 0.5.2b)
breadboards: 1

parts:
  VCC1 = Battery block 9V
  S1 = Pushbutton [package="[THT]"]
  R1 = Resistor [resistance=1k package=THT]
  LED1 = Red LED - 5mm [package="5 mm [THT]"]
  R2 = Resistor [resistance=220 package=THT]

nets:
  N1: VCC1.-, S1.Pin_3, S1.Pin_4
  N2: VCC1.+, R1.Pin_1, LED1.cathode, R2.Pin_1
  N3: S1.Pin_1, S1.Pin_2, R2.Pin_0
  N4: R1.Pin_0, LED1.anode
