# Fritzing sketch CapacitorLED (saved by Fritzing 0.5.2b)
breadboards: 1

parts:
  S1 = Pushbutton [package="[THT]"]
  R1 = Resistor [resistance=1k package=THT]
  VCC1 = Battery block 9V
  C1 = Electrolytic Capacitor [package=THT]
  LED1 = Red LED - 5mm
  R2 = Resistor [resistance=10k package=THT]

nets:
  N1: S1.Pin_1, S1.Pin_2, R1.Pin_0
  N2: S1.Pin_3, S1.Pin_4, LED1.anode
  N3: R1.Pin_1, VCC1.+
  N4: VCC1.-, R2.Pin_1
  N5: C1.-, R2.Pin_0
  N6: C1.+, LED1.cathode
