# Fritzing sketch LEDTransitorBlink (saved by Fritzing 0.4.3b)
breadboards: 1

parts:
  Q1 = npn-Powertransistor [package="TO220 [THT]"]
  C1 = Electrolytic Capacitor [package=THT]
  C1_2 = Electrolytic Capacitor [package=THT]
  LED1 = Red LED - 5mm
  R1 = Resistor [resistance=220 package=THT]
  S1 = Pushbutton [package="[THT]"]
  VCC1 = obsolete Battery
  R1_2 = Resistor [resistance=220 package=THT]
  LED1_2 = Red LED - 5mm
  Q1_2 = npn-Powertransistor [package="TO220 [THT]"]
  Q1_3 = npn-Powertransistor [package="TO220 [THT]"]  # not connected

nets:
  N1: Q1.collector, C1.+, R1.Pin_1
  N2: Q1.emitter, C1.-, VCC1.-, R1_2.Pin_1, Q1_2.emitter
  N3: C1_2.-, Q1_2.base
  N4: C1_2.+, S1.Pin_3, S1.Pin_4
  N5: LED1.anode, R1.Pin_0
  N6: S1.Pin_1, S1.Pin_2, VCC1.+
  N7: R1_2.Pin_0, LED1_2.anode
  N8: LED1_2.cathode, Q1_2.collector
