# Fritzing sketch TiltBallLEDSwitch (saved by Fritzing 0.5.2b)
breadboards: 1

parts:
  LED1 = Red LED - 5mm
  S1 = Tilt Switch [package=THT]
  R1 = Resistor [resistance=1k package=THT]
  VCC1 = Battery block 9V

nets:
  N1: LED1.cathode, VCC1.-
  N2: LED1.anode, R1.Pin_1
  N3: S1.Pin_1, R1.Pin_0
  N4: S1.Pin_2, VCC1.+
