# Fritzing sketch Hall-effect (saved by Fritzing 0.6.2b)
breadboards: 1

parts:
  Arduino1 = Arduino
  U1 = mystery part, 3 pins [chip_label=? spacing=300mil]

nets:
  N1: Arduino1.D2, U1.pin3
  N2: Arduino1.+5V, U1.pin2
  N3: Arduino1.GND, U1.pin1
